// Logisim project SN74.circ as structural Verilog: 6 circuits, main circuit 74193
module _74193 (
  input  CLR,
  input  UP,
  input  DOWN,
  input  nLOAD,
  input  D0,
  input  D1,
  input  D2,
  input  D3,
  output \С0 ,
  output BO,
  output Q0,
  output Q1,
  output Q2,
  output Q3
);

  wire and_1_out, and_2_out, and_3_out, and_4_out, and_5_out, and_6_out, and_7_out, and_8_out, d_ff_1_q,
       d_ff_1_qn, d_ff_2_qn, d_ff_3_qn, d_ff_4_qn, d_ff_5_qn, nand_1_out, nand_2_out, nand_3_out, nand_4_out,
       nand_5_out, nand_6_out, nand_7_out, nand_8_out, nand_9_out, nand_10_out, nand_11_out, nand_12_out,
       nand_13_out, nand_14_out, nand_15_out, not_1_out, not_2_out, not_3_out, not_4_out, not_5_out,
       not_6_out, not_7_out, not_8_out, not_9_out, not_10_out, or_1_out, or_2_out, or_3_out, xor_1_out,
       xor_2_out, xor_3_out, xor_4_out, xor_5_out, xor_6_out;

  not not_1 (not_1_out, CLR);
  not not_2 (not_2_out, nLOAD);
  not not_3 (not_3_out, D0);
  not not_4 (not_4_out, D1);
  not not_5 (not_5_out, D2);
  not not_6 (not_6_out, D3);
  nand nand_1 (nand_1_out, not_2_out, not_3_out);
  nand nand_2 (nand_2_out, not_2_out, not_4_out);
  nand nand_3 (nand_3_out, not_2_out, not_5_out);
  nand nand_4 (nand_4_out, not_2_out, not_6_out);
  and and_1 (and_1_out, not_1_out, not_2_out, D0);
  nand nand_5 (nand_5_out, not_1_out, nand_1_out);
  and and_2 (and_2_out, not_1_out, not_2_out, D1);
  nand nand_6 (nand_6_out, not_1_out, nand_2_out);
  and and_3 (and_3_out, not_1_out, not_2_out, D2);
  nand nand_7 (nand_7_out, not_1_out, nand_3_out);
  and and_4 (and_4_out, D3, not_2_out, not_1_out);
  nand nand_8 (nand_8_out, not_1_out, nand_4_out);
  not not_7 (not_7_out, UP);
  not not_8 (not_8_out, DOWN);
  nand nand_9 (nand_9_out, UP, DOWN);
  not not_9 (not_9_out, UP);
  D_Flip_Flop d_ff_1 (.Q(d_ff_1_q), .Qn(d_ff_1_qn), .preset(not_9_out), .reset(not_10_out));  // open: clk, D
  not not_10 (not_10_out, DOWN);
  xor xor_1 (xor_1_out, Q0, Q1);
  xor xor_2 (xor_2_out, d_ff_2_qn, Q1);
  and and_5 (and_5_out, Q0, Q1);
  xor xor_3 (xor_3_out, and_5_out, Q2);
  and and_6 (and_6_out, d_ff_2_qn, d_ff_3_qn);
  xor xor_4 (xor_4_out, and_6_out, Q2);
  and and_7 (and_7_out, Q0, Q1, Q2);
  xor xor_5 (xor_5_out, and_7_out, Q3);
  and and_8 (and_8_out, d_ff_2_qn, d_ff_3_qn, d_ff_4_qn);
  xor xor_6 (xor_6_out, and_8_out, Q3);
  nand nand_10 (nand_10_out, d_ff_1_q, xor_1_out);
  nand nand_11 (nand_11_out, d_ff_1_qn, xor_2_out);
  nand nand_12 (nand_12_out, d_ff_1_q, xor_3_out);
  nand nand_13 (nand_13_out, d_ff_1_qn, xor_4_out);
  nand nand_14 (nand_14_out, d_ff_1_q, xor_5_out);
  nand nand_15 (nand_15_out, d_ff_1_qn, xor_6_out);
  nand nand_16 (\С0 , Q0, Q1, Q2, Q3, not_7_out);
  nand nand_17 (BO, d_ff_2_qn, d_ff_3_qn, d_ff_4_qn, d_ff_5_qn, not_8_out);
  or or_1 (or_1_out, ~nand_10_out, ~nand_11_out);  // OR_Gate
  or or_2 (or_2_out, ~nand_12_out, ~nand_13_out);  // OR_Gate
  or or_3 (or_3_out, ~nand_14_out, ~nand_15_out);  // OR_Gate
  D_Flip_Flop d_ff_2 (.clk(nand_9_out), .D(d_ff_2_qn), .Q(Q0), .Qn(d_ff_2_qn), .preset(and_1_out), .reset(nand_5_out));
  D_Flip_Flop d_ff_3 (.clk(nand_9_out), .D(or_1_out), .Q(Q1), .Qn(d_ff_3_qn), .preset(and_2_out), .reset(nand_6_out));
  D_Flip_Flop d_ff_4 (.clk(nand_9_out), .D(or_2_out), .Q(Q2), .Qn(d_ff_4_qn), .preset(and_3_out), .reset(nand_7_out));
  D_Flip_Flop d_ff_5 (.clk(nand_9_out), .D(or_3_out), .Q(Q3), .Qn(d_ff_5_qn), .preset(and_4_out), .reset(nand_8_out));
endmodule

module _7493 (
  input  CLKA,
  input  CLKB,
  input  R0,
  input  R1,
  output Q0,
  output Q1,
  output Q2,
  output Q3
);

  wire and_1_out;

  and and_1 (and_1_out, R0, R1);
  J_K_Flip_Flop j_k_ff_1 (.J(1'b1), .clk(CLKA), .K(1'b1), .Q(Q0), .reset(and_1_out));  // open: Qn, preset
  J_K_Flip_Flop j_k_ff_2 (.J(1'b1), .clk(CLKB), .K(1'b1), .Q(Q1), .reset(and_1_out));  // open: Qn, preset
  J_K_Flip_Flop j_k_ff_3 (.J(1'b1), .clk(Q1), .K(1'b1), .Q(Q2), .reset(and_1_out));  // open: Qn, preset
  J_K_Flip_Flop j_k_ff_4 (.J(1'b1), .clk(Q2), .K(1'b1), .Q(Q3), .reset(and_1_out));  // open: Qn, preset
endmodule

module _7474 (
  input  nS,
  input  CLK,
  input  D,
  input  nR,
  output Q,
  output nQ
);

  D_Flip_Flop #(.NegatePresetClear("true")) d_ff_1 (.clk(CLK), .D(D), .Q(Q), .Qn(nQ), .preset(nS), .reset(nR));
endmodule

module _74157 (
  input  A0,
  input  B0,
  input  A1,
  input  B1,
  input  A2,
  input  B2,
  input  A3,
  input  B3,
  input  nG,
  input  nA_B,
  output Y0,
  output Y1,
  output Y2,
  output Y3
);

  wire and_1_out, and_2_out, and_3_out, and_4_out, and_5_out, and_6_out, and_7_out, and_8_out, and_9_out,
       and_10_out, not_1_out;

  not not_1 (not_1_out, nA_B);
  and and_1 (and_1_out, A0, and_9_out);
  and and_2 (and_2_out, B0, and_10_out);
  and and_3 (and_3_out, A1, and_9_out);
  and and_4 (and_4_out, B1, and_10_out);
  and and_5 (and_5_out, A2, and_9_out);
  and and_6 (and_6_out, B2, and_10_out);
  and and_7 (and_7_out, A3, and_9_out);
  and and_8 (and_8_out, B3, and_10_out);
  and and_9 (and_9_out, ~nG, ~nA_B);  // AND_Gate
  and and_10 (and_10_out, ~nG, ~not_1_out);  // AND_Gate
  or or_1 (Y0, and_1_out, and_2_out);
  or or_2 (Y1, and_3_out, and_4_out);
  or or_3 (Y2, and_5_out, and_6_out);
  or or_4 (Y3, and_7_out, and_8_out);
endmodule

module _74257 (
  input  A0,
  input  B0,
  input  A1,
  input  B1,
  input  A2,
  input  B2,
  input  A3,
  input  B3,
  input  nOE,
  input  nA_B,
  output Y0,
  output Y1,
  output Y2,
  output Y3
);

  wire and_1_out, and_2_out, and_3_out, and_4_out, and_5_out, and_6_out, and_7_out, and_8_out, not_1_out,
       not_2_out, or_1_out, or_2_out, or_3_out, or_4_out;

  not not_1 (not_1_out, nOE);
  not not_2 (not_2_out, nA_B);
  and and_1 (and_1_out, A0, not_2_out);
  or or_1 (or_1_out, and_1_out, and_2_out);
  and and_2 (and_2_out, B0, nA_B);
  and and_3 (and_3_out, A1, not_2_out);
  or or_2 (or_2_out, and_3_out, and_4_out);
  and and_4 (and_4_out, B1, nA_B);
  and and_5 (and_5_out, A2, not_2_out);
  or or_3 (or_3_out, and_5_out, and_6_out);
  and and_6 (and_6_out, B2, nA_B);
  and and_7 (and_7_out, A3, not_2_out);
  or or_4 (or_4_out, and_7_out, and_8_out);
  and and_8 (and_8_out, B3, nA_B);
  assign Y0 = not_1_out ? or_1_out : 1'bz;  // Controlled_Buffer controlled_buffer_1
  assign Y1 = not_1_out ? or_2_out : 1'bz;  // Controlled_Buffer controlled_buffer_2
  assign Y2 = not_1_out ? or_3_out : 1'bz;  // Controlled_Buffer controlled_buffer_3
  assign Y3 = not_1_out ? or_4_out : 1'bz;  // Controlled_Buffer controlled_buffer_4
endmodule

module _74393 (
  input  CLR,
  input  nCLK,
  output Q0,
  output Q1,
  output Q2,
  output Q3
);

  wire j_k_ff_1_qn, j_k_ff_2_qn, j_k_ff_3_qn, not_1_out, not_2_out;

  not not_1 (not_1_out, not_2_out);
  not not_2 (not_2_out, CLR);
  J_K_Flip_Flop j_k_ff_1 (.J(1'b1), .clk(nCLK), .K(1'b1), .Q(Q0), .Qn(j_k_ff_1_qn), .reset(not_1_out));  // open: preset
  J_K_Flip_Flop j_k_ff_2 (
    .J(1'b1), .clk(j_k_ff_1_qn), .K(1'b1), .Q(Q1), .Qn(j_k_ff_2_qn), .reset(not_1_out));  // open: preset
  J_K_Flip_Flop j_k_ff_3 (
    .J(1'b1), .clk(j_k_ff_2_qn), .K(1'b1), .Q(Q2), .Qn(j_k_ff_3_qn), .reset(not_1_out));  // open: preset
  J_K_Flip_Flop j_k_ff_4 (.J(1'b1), .clk(j_k_ff_3_qn), .K(1'b1), .Q(Q3), .reset(not_1_out));  // open: Qn, preset
endmodule
