// Logisim project ZX-Penagon.circ as structural Verilog: 2 circuits, main circuit main
module main (
  input  in_1,
  output out_2,
  output out_3
);

  wire not_1_out, VSYNC;

  Generator generator_1 ();  // open: C30, C29, MCLK, C31, nC1, AYCLK, nC25, C25, nC2, HSYNC, C3, C5, FSYNC, SA0, SA1, SA2, SA3, SA4, SA5, SA6, SA7, SA8, SA9, SA10, SA11, SA12, BL
  not not_1 (not_1_out, VSYNC);
  _7474 VSYNC_detector (.nS(not_1_out), .nR(in_1), .Q(out_2), .nQ(out_3));  // open: CLK, D
endmodule

module Generator (
  input  C30,
  input  C29,
  output MCLK,
  output C31,
  output nC1,
  output AYCLK,
  output nC25,
  output C25,
  output nC2,
  output HSYNC,
  output C3,
  output C5,
  output FSYNC,
  output SA0,
  output SA1,
  output SA2,
  output SA3,
  output SA4,
  output SA5,
  output SA6,
  output SA7,
  output SA8,
  output SA9,
  output SA10,
  output SA11,
  output SA12,
  output BL
);

  wire and_1_out, and_2_out, and_3_out, and_4_out, and_5_out, B6, B50, C6, n7493_1_q1, nor_1_out, nor_2_out,
       not_5_out, U5_74193_q0, U5_74193_q1, \U5_74193_с0 , \U10_74192_с0 , U14B_74393_q3, VSYNC;
  wire [1:0] B7__8, B12__13;

  Clock Main_Generator (.out(C31));
  _74193 U5_74193 (
    .CLR(1'b0), .UP(nC25), .DOWN(1'b1), .nLOAD(1'b1), .D0(1'b1), .D1(1'b1), .D2(1'b1), .D3(1'b1),
    .\С0 (\U5_74193_с0 ), .Q0(U5_74193_q0), .Q1(U5_74193_q1), .Q2(SA0), .Q3(SA1));  // open: BO
  _74193 U10_74192 (
    .CLR(1'b0), .UP(\U5_74193_с0 ), .DOWN(1'b1), .nLOAD(\U10_74192_с0 ), .D0(1'b1), .D1(1'b0), .D2(1'b0),
    .D3(1'b0), .\С0 (\U10_74192_с0 ), .Q0(SA2), .Q1(SA3), .Q2(SA4), .Q3(B50));  // open: BO
  _74393 U14A_74393 (.CLR(1'b0), .nCLK(B6), .Q0(B7__8[0]), .Q1(B7__8[1]), .Q2(SA5), .Q3(SA6));
  _74393 U14B_74393 (.CLR(and_2_out), .nCLK(SA6), .Q0(SA7), .Q1(B12__13[0]), .Q2(B12__13[1]), .Q3(U14B_74393_q3));
  _7493 u_7493_1 (.CLKA(HSYNC), .CLKB(C31), .R0(1'b0), .R1(1'b0), .Q0(B6), .Q1(n7493_1_q1), .Q2(nC25), .Q3(AYCLK));
  not not_1 (C25, nC25);
  and and_1 (and_1_out, C25, U5_74193_q0, U5_74193_q1);
  and and_2 (and_2_out, B12__13[0], U14B_74393_q3);
  not not_2 (nC1, n7493_1_q1);
  not not_3 (nC2, and_1_out);
  not not_4 (C3, U5_74193_q1);
  not not_5 (not_5_out, SA2);
  nor nor_1 (nor_1_out, SA3, B50);
  nand nand_1 (HSYNC, not_5_out, nor_1_out);
  and and_3 (and_3_out, nor_1_out, SA4);
  and and_4 (and_4_out, B50, C6);
  and and_5 (and_5_out, B12__13[0], B12__13[1]);
  _74157 U6_74157 (
    .A0(B12__13[0]), .B0(B6), .A1(B12__13[1]), .B1(B7__8[0]), .A2(1'b0), .B2(B7__8[1]), .A3(1'b1),
    .B3(B12__13[0]), .nG(1'b0), .nA_B(C30), .Y0(SA8), .Y1(SA9), .Y2(SA10), .Y3(SA11));
  not not_6 (SA12, nor_2_out);
  nor nor_2 (nor_2_out, B12__13[1], C29);
  _7474 u_7474_1 (.nS(1'b1), .CLK(SA0), .D(and_4_out), .nR(1'b1), .nQ(C5));  // open: Q
  and and_6 (VSYNC, and_5_out, SA6, SA7);
  nor nor_3 (C6, and_5_out, U14B_74393_q3);
  xor xor_1 (FSYNC, HSYNC, VSYNC);
  xor xor_2 (BL, VSYNC, and_3_out);
  // Digital_Oscilloscope #(.nState(29)) digital_oscilloscope_1: pin names not known; wires that end beside it: C31, nC25, C25, SA0, SA1, SA2, SA3, SA4, SA5, SA6, SA7

  assign MCLK = C31;

  // Other names for the same wires on the sheet: SA0__1[1:0] = {SA1, SA0}; SA0_t = SA0; SA2__4[2:0] = {SA4, SA3, SA2};
  //   SA5__6[1:0] = {SA6, SA5}; SA8__11[3:0] = {SA11, SA10, SA9, SA8}
endmodule
