// Logisim project ZXPenagon.circ as structural Verilog
module Genetator (
  input  RT,
  input  C30,
  input  C29,
  output MAINCLK,
  output NC1,
  output NC25,
  output AYCLK,
  output C25,
  output NC2,
  output C3,
  output HSYNC,
  output FSYNC,
  output VSYNC,
  output BL,
  output C5,
  output C6,
  output SA0,
  output SA1,
  output SA2,
  output SA3,
  output SA4,
  output SA5,
  output SA6,
  output SA7,
  output SA8,
  output SA9,
  output SA10,
  output SA11,
  output SA12
);

  wire and_1_out, and_2_out, and_3_out, and_5_out, B6, B7, B8, B12, B13, B50, B51, nor_1_out, nor_3_out,
       not_4_out, sn7493_1_q1, sn74193_1_nco, sn74193_1_q0, sn74193_1_q1, sn74193_2_nco;

  Clock clock_1 (.out(MAINCLK));
  and and_1 (and_1_out, B12, B51);
  not not_1 (C25, NC25);
  SN74193 sn74193_1 (
    .UP(NC25), .DOWN(1'b1), .D0(1'b1), .D1(1'b1), .D2(1'b1), .D3(1'b1), .NLOAD(1'b1), .CLR(1'b0),
    .NCO(sn74193_1_nco), .Q0(sn74193_1_q0), .Q1(sn74193_1_q1), .Q2(SA0), .Q3(SA1));  // open: NBO
  SN74193 sn74193_2 (
    .UP(sn74193_1_nco), .DOWN(1'b1), .D0(1'b1), .D1(1'b0), .D2(1'b0), .D3(1'b0), .NLOAD(sn74193_2_nco),
    .CLR(1'b0), .NCO(sn74193_2_nco), .Q0(SA2), .Q1(SA3), .Q2(SA4), .Q3(B50));  // open: NBO
  SN74393 sn74393_1 (.CLR(1'b0), .NCLK(B6), .Q0(B7), .Q1(B8), .Q2(SA5), .Q3(SA6));
  SN74393 sn74393_2 (.CLR(and_1_out), .NCLK(SA6), .Q0(SA7), .Q1(B12), .Q2(B13), .Q3(B51));
  not not_2 (C3, sn74193_1_q1);
  SN7493 sn7493_1 (
    .CLKA(HSYNC), .CLKB(MAINCLK), .R0(1'b0), .R1(1'b0), .Q0(B6), .Q1(sn7493_1_q1), .Q2(NC25), .Q3(AYCLK));
  not not_3 (NC1, sn7493_1_q1);
  nand nand_1 (NC2, C25, sn74193_1_q0, sn74193_1_q1);
  not not_4 (not_4_out, SA2);
  nor nor_1 (nor_1_out, SA3, B50);
  and and_2 (and_2_out, B50, C6);
  and and_3 (and_3_out, B12, B13);
  and and_4 (VSYNC, and_3_out, SA6, SA7);
  nand nand_2 (HSYNC, not_4_out, nor_1_out);
  and and_5 (and_5_out, nor_1_out, SA4);
  nor nor_2 (C6, and_3_out, B51);
  xor xor_1 (FSYNC, HSYNC, VSYNC);
  xor xor_2 (BL, VSYNC, and_5_out);
  SN7474 sn7474_1 (.NS(RT), .CLK(SA0), .D(and_2_out), .NR(1'b1), .Q(C5));  // open: NQ
  SN74157 sn74157_1 (
    .A0(B12), .B0(B6), .A1(B13), .B1(B7), .A2(1'b0), .B2(B8), .A3(1'b1), .B3(B12), .NG(1'b0), .NAB(C30),
    .Y0(SA8), .Y1(SA9), .Y2(SA10), .Y3(SA11));
  nor nor_3 (nor_3_out, B13, C29);
  not not_5 (SA12, nor_3_out);
endmodule
