// Logisim project SN74.circ as structural Verilog: 7 circuits, main circuit SN74193
module SN74193 (
  input  UP,
  input  DOWN,
  input  D0,
  input  D1,
  input  D2,
  input  D3,
  input  NLOAD,
  input  CLR,
  output NCO,
  output NBO,
  output Q0,
  output Q1,
  output Q2,
  output Q3
);

  wire and_1_out, and_2_out, and_3_out, and_4_out, and_5_out, and_6_out, and_7_out, and_8_out, and_9_out,
       and_10_out, and_11_out, and_12_out, and_13_out, and_14_out, d_ff_1_qn, d_ff_2_qn, d_ff_3_qn,
       d_ff_4_qn, nor_1_out, nor_2_out, nor_3_out, nor_4_out, not_1_out, not_2_out, not_3_out, not_4_out,
       or_1_out, or_2_out, or_3_out, or_4_out;

  not not_1 (not_1_out, UP);
  not not_2 (not_2_out, DOWN);
  not not_3 (not_3_out, NLOAD);
  not not_4 (not_4_out, CLR);
  and and_1 (and_1_out, D0, not_3_out, not_4_out);
  nor nor_1 (nor_1_out, not_2_out, not_1_out);
  and and_2 (and_2_out, D1, not_3_out, not_4_out);
  and and_3 (and_3_out, not_2_out, d_ff_1_qn);
  nor nor_2 (nor_2_out, and_3_out, and_4_out);
  and and_4 (and_4_out, Q0, not_1_out);
  and and_5 (and_5_out, D2, not_3_out, not_4_out);
  and and_6 (and_6_out, not_2_out, d_ff_1_qn, d_ff_2_qn);
  nor nor_3 (nor_3_out, and_6_out, and_7_out);
  and and_7 (and_7_out, Q1, Q0, not_1_out);
  and and_8 (and_8_out, D3, not_3_out, not_4_out);
  and and_9 (and_9_out, not_2_out, d_ff_1_qn, d_ff_2_qn, d_ff_3_qn);
  nor nor_4 (nor_4_out, and_9_out, and_10_out);
  and and_10 (and_10_out, Q2, Q1, Q0, not_1_out);
  and and_11 (and_11_out, ~and_1_out, not_3_out);  // AND_Gate
  and and_12 (and_12_out, ~and_2_out, not_3_out);  // AND_Gate
  and and_13 (and_13_out, ~and_5_out, not_3_out);  // AND_Gate
  and and_14 (and_14_out, ~and_8_out, not_3_out);  // AND_Gate
  D_Flip_Flop d_ff_1 (.D(d_ff_1_qn), .clk(nor_1_out), .Q(Q0), .Qn(d_ff_1_qn), .preset(and_1_out), .reset(or_1_out));
  or or_1 (or_1_out, and_11_out, ~not_4_out);  // OR_Gate
  D_Flip_Flop d_ff_2 (.D(d_ff_2_qn), .clk(nor_2_out), .Q(Q1), .Qn(d_ff_2_qn), .preset(and_2_out), .reset(or_2_out));
  or or_2 (or_2_out, and_12_out, ~not_4_out);  // OR_Gate
  D_Flip_Flop d_ff_3 (.D(d_ff_3_qn), .clk(nor_3_out), .Q(Q2), .Qn(d_ff_3_qn), .preset(and_5_out), .reset(or_3_out));
  or or_3 (or_3_out, and_13_out, ~not_4_out);  // OR_Gate
  D_Flip_Flop d_ff_4 (.D(d_ff_4_qn), .clk(nor_4_out), .Q(Q3), .Qn(d_ff_4_qn), .preset(and_8_out), .reset(or_4_out));
  or or_4 (or_4_out, and_14_out, ~not_4_out);  // OR_Gate
  nand nand_1 (NCO, Q3, Q2, Q1, Q0, not_1_out);
  nand nand_2 (NBO, d_ff_4_qn, d_ff_3_qn, d_ff_2_qn, d_ff_1_qn, not_2_out);
endmodule

module SN7474 (
  input  NS,
  input  CLK,
  input  D,
  input  NR,
  output Q,
  output NQ
);

  wire nand_1_out, nand_2_out, nand_3_out, nand_4_out;

  nand nand_1 (nand_1_out, NS, nand_4_out, nand_2_out);
  nand nand_2 (nand_2_out, nand_1_out, NR, CLK);
  nand nand_3 (nand_3_out, nand_2_out, CLK, nand_4_out);
  nand nand_4 (nand_4_out, nand_3_out, NR, D);
  nand nand_5 (Q, NS, nand_2_out, NQ);
  nand nand_6 (NQ, Q, NR, nand_3_out);

  // Notes on the sheet:
  //   NS: initial=0x1
  //   NR: initial=0x1
endmodule

module SN74257 (
  input  A0,
  input  B0,
  input  A1,
  input  B1,
  input  A2,
  input  B2,
  input  A3,
  input  B3,
  input  NAB,
  input  NOE,
  output Y0,
  output Y1,
  output Y2,
  output Y3
);

  wire and_1_out, and_2_out, and_3_out, and_4_out, and_5_out, and_6_out, and_7_out, and_8_out, not_1_out,
       not_2_out, or_1_out, or_2_out, or_3_out, or_4_out;

  not not_1 (not_1_out, NAB);
  not not_2 (not_2_out, NOE);
  and and_1 (and_1_out, A0, not_1_out);
  or or_1 (or_1_out, and_1_out, and_2_out);
  and and_2 (and_2_out, B0, NAB);
  and and_3 (and_3_out, A1, not_1_out);
  or or_2 (or_2_out, and_3_out, and_4_out);
  and and_4 (and_4_out, B1, NAB);
  and and_5 (and_5_out, A2, not_1_out);
  or or_3 (or_3_out, and_5_out, and_6_out);
  and and_6 (and_6_out, B2, NAB);
  and and_7 (and_7_out, A3, not_1_out);
  or or_4 (or_4_out, and_7_out, and_8_out);
  and and_8 (and_8_out, B3, NAB);
  assign Y0 = not_2_out ? or_1_out : 1'bz;  // Controlled_Buffer controlled_buffer_1
  assign Y1 = not_2_out ? or_2_out : 1'bz;  // Controlled_Buffer controlled_buffer_2
  assign Y2 = not_2_out ? or_3_out : 1'bz;  // Controlled_Buffer controlled_buffer_3
  assign Y3 = not_2_out ? or_4_out : 1'bz;  // Controlled_Buffer controlled_buffer_4
endmodule

module SN74393 (
  input  CLR,
  input  NCLK,
  output Q0,
  output Q1,
  output Q2,
  output Q3
);

  wire d_ff_1_qn, d_ff_2_qn, d_ff_3_qn, d_ff_4_qn;

  D_Flip_Flop #(.trigger("falling")) d_ff_1 (
    .D(d_ff_1_qn), .clk(NCLK), .Q(Q0), .Qn(d_ff_1_qn), .reset(CLR));  // open: preset
  D_Flip_Flop #(.trigger("falling")) d_ff_2 (
    .D(d_ff_2_qn), .clk(Q0), .Q(Q1), .Qn(d_ff_2_qn), .reset(CLR));  // open: preset
  D_Flip_Flop #(.trigger("falling")) d_ff_3 (
    .D(d_ff_3_qn), .clk(Q1), .Q(Q2), .Qn(d_ff_3_qn), .reset(CLR));  // open: preset
  D_Flip_Flop #(.trigger("falling")) d_ff_4 (
    .D(d_ff_4_qn), .clk(Q2), .Q(Q3), .Qn(d_ff_4_qn), .reset(CLR));  // open: preset
endmodule

module SN7493 (
  input  CLKA,
  input  CLKB,
  input  R0,
  input  R1,
  output Q0,
  output Q1,
  output Q2,
  output Q3
);

  wire and_1_out, d_ff_1_qn, d_ff_2_qn, d_ff_3_qn, d_ff_4_qn;

  and and_1 (and_1_out, R0, R1);
  D_Flip_Flop #(.trigger("falling")) d_ff_1 (
    .D(d_ff_1_qn), .clk(CLKA), .Q(Q0), .Qn(d_ff_1_qn), .reset(and_1_out));  // open: preset
  D_Flip_Flop #(.trigger("falling")) d_ff_2 (
    .D(d_ff_2_qn), .clk(CLKB), .Q(Q1), .Qn(d_ff_2_qn), .reset(and_1_out));  // open: preset
  D_Flip_Flop #(.trigger("falling")) d_ff_3 (
    .D(d_ff_3_qn), .clk(Q1), .Q(Q2), .Qn(d_ff_3_qn), .reset(and_1_out));  // open: preset
  D_Flip_Flop #(.trigger("falling")) d_ff_4 (
    .D(d_ff_4_qn), .clk(Q2), .Q(Q3), .Qn(d_ff_4_qn), .reset(and_1_out));  // open: preset
endmodule

module SN74157 (
  input  A0,
  input  B0,
  input  A1,
  input  B1,
  input  A2,
  input  B2,
  input  A3,
  input  B3,
  input  NG,
  input  NAB,
  output Y0,
  output Y1,
  output Y2,
  output Y3
);

  wire and_1_out, and_2_out, and_3_out, and_4_out, and_5_out, and_6_out, and_7_out, and_8_out, and_9_out,
       and_10_out;

  and and_1 (and_1_out, ~NG, ~NAB);  // AND_Gate
  and and_2 (and_2_out, ~NG, NAB);  // AND_Gate
  and and_3 (and_3_out, A0, and_1_out);
  and and_4 (and_4_out, B0, and_2_out);
  and and_5 (and_5_out, A1, and_1_out);
  and and_6 (and_6_out, B1, and_2_out);
  and and_7 (and_7_out, A2, and_1_out);
  and and_8 (and_8_out, B2, and_2_out);
  and and_9 (and_9_out, A3, and_1_out);
  and and_10 (and_10_out, B3, and_2_out);
  or or_1 (Y0, and_3_out, and_4_out);
  or or_2 (Y1, and_5_out, and_6_out);
  or or_3 (Y2, and_7_out, and_8_out);
  or or_4 (Y3, and_9_out, and_10_out);
endmodule

module SN74153 (
  input  A0,
  input  B0,
  input  C0,
  input  D0,
  input  G0,
  input  S0,
  input  S1,
  input  G1,
  input  A1,
  input  B1,
  input  C1,
  input  C2,
  output Y0,
  output out_14
);

  wire and_1_out, and_2_out, and_3_out, and_4_out, and_5_out, and_6_out, and_7_out, and_8_out, not_1_out,
       not_2_out, not_3_out, not_4_out, not_5_out, not_6_out;

  not not_1 (not_1_out, G0);
  not not_2 (not_2_out, S0);
  not not_3 (not_3_out, not_2_out);
  not not_4 (not_4_out, S1);
  not not_5 (not_5_out, not_4_out);
  not not_6 (not_6_out, G1);
  and and_1 (and_1_out, A0, not_2_out, not_4_out, not_1_out);
  and and_2 (and_2_out, B0, not_4_out, not_3_out, not_1_out);
  and and_3 (and_3_out, C0, not_2_out, not_5_out, not_1_out);
  and and_4 (and_4_out, D0, not_3_out, not_5_out, not_1_out);
  and and_5 (and_5_out, not_6_out, not_2_out, not_4_out, A1);
  and and_6 (and_6_out, not_6_out, not_4_out, not_3_out, B1);
  and and_7 (and_7_out, not_6_out, not_2_out, not_5_out, C1);
  and and_8 (and_8_out, not_6_out, not_2_out, not_5_out, C2);
  or or_1 (Y0, and_1_out, and_2_out, and_3_out, and_4_out);
  or or_2 (out_14, and_5_out, and_6_out, and_7_out, and_8_out);
endmodule
