// Logisim project ZXPenagon.circ as structural Verilog: 4 circuits, main circuit main
module main (
  input  RT
);

  wire AYCLK, BL, C3, C5, C6, C25, C29, C30, FSYNC, HSYNC, MAINCLK, NC1, NC2, NC25, NCAS, RAS, VSYNC;
  wire [0:0] SA12;
  wire [3:0] SA0_3, SA4_7, SA8_11;

  Genetator genetator_1 (
    .RT(RT), .C30(C30), .C29(C29), .MAINCLK(MAINCLK), .NC1(NC1), .NC25(NC25), .AYCLK(AYCLK), .C25(C25),
    .NC2(NC2), .C3(C3), .HSYNC(HSYNC), .FSYNC(FSYNC), .VSYNC(VSYNC), .BL(BL), .C5(C5), .C6(C6),
    .SA0(SA0_3[0]), .SA1(SA0_3[1]), .SA2(SA0_3[2]), .SA3(SA0_3[3]), .SA4(SA4_7[0]), .SA5(SA4_7[1]),
    .SA6(SA4_7[2]), .SA7(SA4_7[3]), .SA8(SA8_11[0]), .SA9(SA8_11[1]), .SA10(SA8_11[2]), .SA11(SA8_11[3]),
    .SA12(SA12[0]));
  MemorySignal memorysignal_1 (.RT(RT), .MAINCLK(MAINCLK), .C25(C25), .RAS(RAS), .NCAS(NCAS));
  MemorySharing memorysharing_1 (
    .NRD(1'b1), .RAS(RAS), .RT(RT), .NRFSH(1'b0), .NCAS(NCAS), .NMREQ(1'b1), .A14(1'b0), .A15(1'b0),
    .C29(C29), .C30(C30));  // open: C19, C16, C20, CPU, DISPLAY, C17, C18, NFQUATER
  Hex_Digit_Display hex_digit_display_1 (.value({3'b000, SA12[0]}));  // open: dp
  Hex_Digit_Display hex_digit_display_2 (.value(SA8_11));  // open: dp
  Hex_Digit_Display hex_digit_display_3 (.value(SA4_7));  // open: dp
  Hex_Digit_Display hex_digit_display_4 (.value(SA0_3));  // open: dp
  // Digital_Oscilloscope RAS_NCAS: pin names not known; wires that end beside it: MAINCLK, RAS, NCAS

  // Notes on the sheet:
  //   SCREEN ADDRRES
endmodule

module Genetator (
  input  RT,
  input  C30,
  input  C29,
  output MAINCLK,
  output NC1,
  output NC25,
  output AYCLK,
  output C25,
  output NC2,
  output C3,
  output HSYNC,
  output FSYNC,
  output VSYNC,
  output BL,
  output C5,
  output C6,
  output SA0,
  output SA1,
  output SA2,
  output SA3,
  output SA4,
  output SA5,
  output SA6,
  output SA7,
  output SA8,
  output SA9,
  output SA10,
  output SA11,
  output SA12
);

  wire and_1_out, and_2_out, and_3_out, and_5_out, B6, B7, B8, B12, B13, B50, B51, nor_1_out, nor_3_out,
       not_4_out, sn7493_1_q1, sn74193_1_nco, sn74193_1_q0, sn74193_1_q1, sn74193_2_nco, undriven;

  Clock clock_1 (.out(MAINCLK));
  and and_1 (and_1_out, B12, B51);
  not not_1 (C25, NC25);
  SN74193 sn74193_1 (
    .UP(NC25), .DOWN(1'b1), .D0(1'b1), .D1(1'b1), .D2(1'b1), .D3(1'b1), .NLOAD(1'b1), .CLR(1'b0),
    .NCO(sn74193_1_nco), .Q0(sn74193_1_q0), .Q1(sn74193_1_q1), .Q2(SA0), .Q3(SA1));  // open: NBO
  SN74193 sn74193_2 (
    .UP(sn74193_1_nco), .DOWN(1'b1), .D0(1'b1), .D1(1'b0), .D2(1'b0), .D3(1'b0), .NLOAD(sn74193_2_nco),
    .CLR(1'b0), .NCO(sn74193_2_nco), .Q0(SA2), .Q1(SA3), .Q2(SA4), .Q3(B50));  // open: NBO
  SN74393 sn74393_1 (.CLR(1'b0), .NCLK(B6), .Q0(B7), .Q1(B8), .Q2(SA5), .Q3(SA6));
  SN74393 sn74393_2 (.CLR(and_1_out), .NCLK(SA6), .Q0(SA7), .Q1(B12), .Q2(B13), .Q3(B51));
  not not_2 (C3, sn74193_1_q1);
  SN7493 sn7493_1 (
    .CLKA(HSYNC), .CLKB(MAINCLK), .R0(1'b0), .R1(1'b0), .Q0(B6), .Q1(sn7493_1_q1), .Q2(NC25), .Q3(AYCLK));
  not not_3 (NC1, sn7493_1_q1);
  nand nand_1 (NC2, C25, sn74193_1_q0, sn74193_1_q1);
  not not_4 (not_4_out, SA2);
  nor nor_1 (nor_1_out, SA3, B50);
  and and_2 (and_2_out, B50, C6);
  and and_3 (and_3_out, B12, B13);
  and and_4 (VSYNC, and_3_out, SA6, SA7);
  nand nand_2 (HSYNC, not_4_out, nor_1_out);
  and and_5 (and_5_out, nor_1_out, SA4);
  nor nor_2 (C6, and_3_out, B51);
  xor xor_1 (FSYNC, HSYNC, VSYNC);
  xor xor_2 (BL, VSYNC, and_5_out);
  SN7474 sn7474_1 (.NS(RT), .CLK(SA0), .D(and_2_out), .NR(1'b1), .Q(C5));  // open: NQ
  SN74157 sn74157_1 (
    .A0(B12), .B0(B6), .A1(B13), .B1(B7), .A2(1'b0), .B2(B8), .A3(undriven), .B3(B12), .NG(1'b0), .NAB(C30),
    .Y0(SA8), .Y1(SA9), .Y2(SA10), .Y3(SA11));
  nor nor_3 (nor_3_out, B13, C29);
  not not_5 (SA12, nor_3_out);
endmodule

module MemorySignal (
  input  RT,
  input  MAINCLK,
  input  C25,
  output RAS,
  output NCAS
);

  SN7474 sn7474_1 (.NS(RT), .CLK(MAINCLK), .D(C25), .NR(1'b1), .Q(RAS));  // open: NQ
  SN7474 sn7474_2 (.NS(RT), .CLK(MAINCLK), .D(RAS), .NR(1'b1), .NQ(NCAS));  // open: Q
endmodule

module MemorySharing (
  input  NRD,
  input  RAS,
  input  RT,
  input  NRFSH,
  input  NCAS,
  input  NMREQ,
  input  A14,
  input  A15,
  output C19,
  output C16,
  output C20,
  output CPU,
  output DISPLAY,
  output C29,
  output C17,
  output C30,
  output C18,
  output NFQUATER
);

  wire and_1_out, and_2_out, and_3_out, nand_2_out, xor_1_out;

  or or_1 (NFQUATER, A14, A15);
  and and_1 (and_1_out, ~NMREQ, NFQUATER);  // AND_Gate
  nand nand_1 (C19, ~NRD, and_1_out);  // NAND_Gate
  nand nand_2 (nand_2_out, NRD, and_1_out);
  and and_2 (and_2_out, NRFSH, and_1_out, DISPLAY);
  nand nand_3 (C20, RAS, CPU);
  SN7474 sn7474_1 (.NS(RT), .CLK(NCAS), .D(and_2_out), .NR(1'b1), .Q(CPU), .NQ(DISPLAY));
  or or_2 (C16, nand_2_out, C20);
  xor xor_1 (xor_1_out, C29, DISPLAY);
  SN7474 sn7474_2 (.NS(RT), .CLK(NCAS), .D(xor_1_out), .NR(1'b1), .Q(C29), .NQ(C30));
  and and_3 (and_3_out, DISPLAY, RAS);
  nand nand_4 (C17, C29, and_3_out);
  nand nand_5 (C18, C30, and_3_out);
endmodule
