// Logisim project ram_rom_control.circ as structural Verilog: 1 circuit, main circuit main
module main (
  input  NRD,
  input  RAS,
  input  CPU,
  input  NMREQ,
  input  A14,
  input  A15
);

  wire and_1_out, nand_1_out, nand_2_out, nand_3_out, not_1_out, not_2_out, or_1_out, or_2_out;

  not not_1 (not_1_out, NRD);
  not not_2 (not_2_out, NMREQ);
  and and_1 (and_1_out, not_2_out, or_1_out);
  or or_1 (or_1_out, A14, A15);
  nand nand_1 (nand_1_out, not_1_out, and_1_out);
  nand nand_2 (nand_2_out, not_1_out, and_1_out);
  nand nand_3 (nand_3_out, RAS, CPU);
  or or_2 (or_2_out, nand_2_out, nand_3_out);
  // Probe on and_1_out
  // Probe on or_1_out
  // Probe on nand_1_out
  // Probe on or_2_out
  // Probe on nand_3_out
endmodule
