// Logisim project port_dekoder.circ as structural Verilog: 1 circuit, main circuit main
module main (
  input  NRD,
  input  NDI_ULA,
  input  NWR,
  input  NIORQ,
  input  A1,
  input  A0,
  input  DI_32765,
  input  A5,
  input  A7,
  input  NM1,
  input  A14,
  input  A15,
  output NIN254,
  output NOUT254,
  output NINKMST,
  output CS_32765,
  output BC1,
  output BDIR
);

  wire I1_out, I2_out, I3_out, I4_out, I5_out, I6_out, I7_out, I8_out, I9_out, I11_out, I12_out, I13_out,
       nand_1_out, nand_2_out, nor_1_out, nor_2_out, nor_3_out, nor_4_out, or_1_out, or_2_out, or_3_out,
       or_4_out, or_5_out, or_6_out, or_7_out;

  buf I8 (I8_out, NRD);
  buf I12 (I12_out, NDI_ULA);
  buf I9 (I9_out, NWR);
  buf I7 (I7_out, NIORQ);
  buf I2 (I2_out, A1);
  buf I1 (I1_out, A0);
  buf I13 (I13_out, DI_32765);
  buf I3 (I3_out, A5);
  buf I4 (I4_out, A7);
  buf I11 (I11_out, NM1);
  buf I5 (I5_out, A14);
  buf I6 (I6_out, A15);
  or or_1 (or_1_out, I8_out, or_3_out);
  or or_2 (or_2_out, I9_out, or_3_out);
  or or_3 (or_3_out, I12_out, I1_out, I7_out, ~I3_out, ~I4_out, ~I2_out);  // OR_Gate
  or or_4 (or_4_out, I8_out, I7_out, ~I1_out, ~I2_out, I3_out, I4_out);  // OR_Gate
  or or_5 (or_5_out, I2_out, I6_out, ~I1_out, ~I5_out);  // OR_Gate
  or or_6 (or_6_out, I13_out, I7_out, I9_out);
  or or_7 (or_7_out, ~I3_out, ~I4_out);  // OR_Gate
  nor nor_1 (nor_1_out, ~I3_out, ~I4_out, I2_out, I7_out);  // NOR_Gate
  nor nor_2 (nor_2_out, or_5_out, or_6_out, or_7_out);
  nand nand_1 (nand_1_out, I11_out, I5_out);
  nand nand_2 (nand_2_out, nor_1_out, I6_out);
  nor nor_3 (nor_3_out, nand_1_out, nand_2_out);
  nor nor_4 (nor_4_out, nand_2_out, I9_out);
  buf OP14 (NIN254, or_1_out);
  buf O15 (NOUT254, or_2_out);
  buf O19 (NINKMST, or_4_out);
  buf O16 (CS_32765, nor_2_out);
  buf O17 (BC1, nor_3_out);
  buf O18 (BDIR, nor_4_out);
endmodule
