// Logisim project video_512k.circ as structural Verilog: 1 circuit, main circuit main
module main (
  input  in_1,
  input  FLASH_BIT,
  input  SERDATA,
  input  PA6,
  input  PA7,
  input  DI512K,
  output Q0,
  output Q1,
  output Q2,
  output Q3,
  output MUX,
  output GPA6,
  output GPA7
);

  wire and_1_out, and_2_out, and_3_out, and_4_out, and_5_out, and_6_out, and_7_out, and_8_out, and_9_out,
       and_10_out, I1_out, I2_out, I3_out, I4_out, I5_out, I6_out, nand_1_out, or_1_out, or_2_out, or_3_out,
       T1_q, T1_qn, T2_q, T2_qn, T3_2_q, T3_2_qn, T3_q, T3_qn, xor_1_out;

  buf I1 (I1_out, in_1);
  buf I2 (I2_out, FLASH_BIT);
  buf I3 (I3_out, SERDATA);
  buf I4 (I4_out, PA6);
  buf I5 (I5_out, PA7);
  buf I6 (I6_out, DI512K);
  buf O16 (Q0, T1_q);
  D_Flip_Flop T1 (.clk(I1_out), .D(T1_qn), .Q(T1_q), .Qn(T1_qn));  // open: preset, reset
  and and_1 (and_1_out, T2_q, T1_qn);
  and and_2 (and_2_out, T1_q, T2_qn);
  or or_1 (or_1_out, and_1_out, and_2_out);
  D_Flip_Flop T2 (.clk(I1_out), .D(or_1_out), .Q(T2_q), .Qn(T2_qn));  // open: preset, reset
  and and_3 (and_3_out, T2_q, T1_q);
  buf Q17 (Q1, T2_q);
  nand nand_1 (nand_1_out, T3_2_q, I2_out);
  and and_4 (and_4_out, I4_out, I6_out);
  and and_5 (and_5_out, I5_out, I6_out);
  and and_6 (and_6_out, T3_q, ~and_3_out);  // AND_Gate
  and and_7 (and_7_out, T3_qn, and_3_out);
  xor xor_1 (xor_1_out, nand_1_out, I3_out);
  or or_2 (or_2_out, and_6_out, and_7_out);
  D_Flip_Flop T3 (.clk(I1_out), .D(or_2_out), .Q(T3_q), .Qn(T3_qn));  // open: preset, reset
  and and_8 (and_8_out, T3_q, and_3_out);
  buf Q18 (Q2, T3_q);
  and and_9 (and_9_out, T3_2_q, ~and_8_out);  // AND_Gate
  and and_10 (and_10_out, T3_2_qn, and_8_out);
  or or_3 (or_3_out, and_9_out, and_10_out);
  D_Flip_Flop T3_2 (.clk(I1_out), .D(or_3_out), .Q(T3_2_q), .Qn(T3_2_qn));  // open: preset, reset
  buf Q19 (Q3, T3_2_q);
  buf _15 (MUX, xor_1_out);
  buf buffer_1 (GPA6, and_4_out);
  buf _13 (GPA7, and_5_out);
endmodule
