// Logisim project sn74xx193.circ as structural Verilog: 1 circuit, main circuit main
module main (
  input  D0,
  input  DOWN,
  input  UP,
  input  D1,
  input  D2,
  input  D3,
  input  CLR,
  input  NLOAD
);

  wire and_1_out, and_2_out, and_3_out, and_4_out, and_5_out, and_6_out, nand_1_out, nand_2_out, nand_3_out,
       nand_4_out, nand_5_out, nand_6_out, nand_7_out, nand_8_out, nand_9_out, nand_10_out, not_1_out,
       not_2_out, not_3_out, not_4_out, not_5_out, not_6_out, not_7_out, not_8_out, or_1_out, or_2_out,
       or_3_out, or_4_out, or_5_out, or_6_out, or_7_out, or_8_out, t_ff_1_qn, t_ff_2_qn, t_ff_3_qn, t_ff_4_qn;
  wire [3:0] t_ff_1_q;

  not not_1 (not_1_out, DOWN);
  not not_2 (not_2_out, UP);
  not not_3 (not_3_out, CLR);
  not not_4 (not_4_out, NLOAD);
  and and_1 (and_1_out, not_1_out, t_ff_1_qn);
  and and_2 (and_2_out, t_ff_1_q[0], not_2_out);
  and and_3 (and_3_out, not_1_out, t_ff_1_qn, t_ff_2_qn);
  and and_4 (and_4_out, t_ff_1_q[0], t_ff_1_q[1], not_2_out);
  and and_5 (and_5_out, not_1_out, t_ff_1_qn, t_ff_2_qn, t_ff_3_qn);
  and and_6 (and_6_out, t_ff_1_q[0], t_ff_1_q[1], t_ff_1_q[2], not_2_out);
  nand nand_1 (nand_1_out, D0, not_4_out, not_3_out);
  or or_1 (or_1_out, not_1_out, not_2_out);
  nand nand_2 (nand_2_out, D1, not_4_out, not_3_out);
  or or_2 (or_2_out, and_1_out, and_2_out);
  nand nand_3 (nand_3_out, D2, not_4_out, not_3_out);
  or or_3 (or_3_out, and_3_out, and_4_out);
  nand nand_4 (nand_4_out, D3, not_4_out, not_3_out);
  or or_4 (or_4_out, and_5_out, and_6_out);
  nand nand_5 (nand_5_out, not_1_out, t_ff_4_qn, t_ff_3_qn, t_ff_2_qn, t_ff_1_qn);
  nand nand_6 (nand_6_out, not_2_out, t_ff_1_q[3], t_ff_1_q[2], t_ff_1_q[1], t_ff_1_q[0]);
  nand nand_7 (nand_7_out, nand_1_out, not_4_out);
  nand nand_8 (nand_8_out, nand_2_out, not_4_out);
  nand nand_9 (nand_9_out, nand_3_out, not_4_out);
  nand nand_10 (nand_10_out, nand_4_out, not_4_out);
  not not_5 (not_5_out, nand_1_out);
  T_Flip_Flop #(.trigger("falling")) t_ff_1 (
    .T(1'b1), .clk(or_1_out), .Q(t_ff_1_q[0]), .Qn(t_ff_1_qn), .reset(or_5_out), .preset(not_5_out));
  or or_5 (or_5_out, ~not_3_out, ~nand_7_out);  // OR_Gate
  not not_6 (not_6_out, nand_2_out);
  T_Flip_Flop #(.trigger("falling")) t_ff_2 (
    .T(1'b1), .clk(or_2_out), .Q(t_ff_1_q[1]), .Qn(t_ff_2_qn), .reset(or_6_out), .preset(not_6_out));
  or or_6 (or_6_out, ~not_3_out, ~nand_8_out);  // OR_Gate
  not not_7 (not_7_out, nand_3_out);
  T_Flip_Flop #(.trigger("falling")) t_ff_3 (
    .T(1'b1), .clk(or_3_out), .Q(t_ff_1_q[2]), .Qn(t_ff_3_qn), .reset(or_7_out), .preset(not_7_out));
  or or_7 (or_7_out, ~not_3_out, ~nand_9_out);  // OR_Gate
  not not_8 (not_8_out, nand_4_out);
  T_Flip_Flop #(.trigger("falling")) t_ff_4 (
    .T(1'b1), .clk(or_4_out), .Q(t_ff_1_q[3]), .Qn(t_ff_4_qn), .reset(or_8_out), .preset(not_8_out));
  or or_8 (or_8_out, ~not_3_out, ~nand_10_out);  // OR_Gate
  // Probe on nand_5_out
  // Probe on nand_6_out
  // Probe on t_ff_1_q[0]
  // Probe on t_ff_1_q[1]
  // Probe on t_ff_1_q[2]
  // Probe on t_ff_1_q[3]
  Hex_Digit_Display hex_digit_display_1 (.value(t_ff_1_q));  // open: dp
endmodule
