// Logisim project wakwup.circ as structural Verilog: 1 circuit, main circuit main
module main (
  input  in_1
);

  wire clock_1_out, nand_1_out, nand_2_out, nand_3_out;
  wire [3:0] counter_1_q;

  Clock clock_1 (.out(clock_1_out));
  Counter #(.max('hf), .trigger("falling"), .width(4)) counter_1 (
    .clr(in_1), .clk(nand_1_out), .Q(counter_1_q));  // open: load, up, count, D, carry
  nand nand_1 (nand_1_out, clock_1_out, nand_2_out);
  nand nand_2 (nand_2_out, counter_1_q[3], counter_1_q[2]);
  nand nand_3 (nand_3_out, counter_1_q[1], counter_1_q[2]);
  // Digital_Oscilloscope #(.nState(16)) digital_oscilloscope_1: pin names not known; wires that end beside it: clock_1_out, nand_1_out, nand_3_out
endmodule
